# Fritzing sketch schematic-attiny85-i2c-rgb (saved by Fritzing 0.9.2b)
circuit board: 1.52367cm x 1.57858cm
breadboards: 1

parts:
  U1 = attiny85 [package=dip]
  LED = RGB LED (com. cathode, rgb) [package="5 mm [THT]"]
  i2c = female pin header, 2 pins [form="♀ (female)"]
  R220 = Resistor [tolerance=±5% resistance=220 package=THT]
  Power = female pin header, 2 pins [form="♀ (female)"]

nets:
  N1: U1.Pin_2, LED.green_anode
  N2: U1.Pin_3, LED.blue_anode
  N3: U1.Pin_4, R220.Pin_1, Power.pin1
  N4: U1.Pin_5, i2c.pin2
  N5: U1.Pin_6, LED.red_anode
  N6: U1.Pin_7, i2c.pin1
  N7: U1.Pin_8, Power.pin2
  N8: LED.common_cathode, R220.Pin_0

notes:
  +
  -
  RgBG
